// Logisim project m1_37069.circ as structural Verilog
module NotGate (
  input  x,
  output xNOT
);

  Pull_Resistor pull_resistor_1 (.node(xNOT));
  Transistor transistor_1 (.in(1'b1), .out(xNOT), .gate(x));
endmodule

module NorGate (
  input  x,
  input  y,
  output xNORy
);

  wire transistor_1_out;

  Transistor transistor_1 (.in(1'b1), .out(transistor_1_out), .gate(x));
  Pull_Resistor pull_resistor_1 (.node(xNORy));
  Transistor transistor_2 (.in(transistor_1_out), .out(xNORy), .gate(y));
endmodule

module AndGate (
  input  x,
  input  y,
  output xANDy
);

  wire transistor_1_out;

  Transistor transistor_1 (.in(1'b1), .out(transistor_1_out), .gate(x));
  Transistor transistor_2 (.in(transistor_1_out), .out(xANDy), .gate(y));
  Pull_Resistor pull_resistor_1 (.node(xANDy));
endmodule
